# Fritzing sketch ARD_PROTO (saved by Fritzing 0.9.3b)

parts:
  U3 = ESP8266 WiFi Module [part_number=ESP8266]
  F1 = Fan - Ventilador [package=THT]
  Part1 = Arduino Uno (Rev3)
  Part2 = Arduino Nano (Rev3.0)
  RHT1 = Humidity and Temperature Sensor RHT03
  R1 = Resistor [tolerance=±5% resistance=220 package="0805 [SMD]"]

nets:
  N1: U3.RXD, Part1.D1/TX
  VCC: U3.VCC, Part1.3V3
  GND: U3.GND, F1.GND, Part1.GND, Part2.GND, RHT1.GND_2
  N2: U3.TXD, Part1.D0/RX
  N3: F1.5V, Part1.D11_PWM/MOSI
  5V: Part1.5V, Part2.VIN
  N4: Part2.D2, RHT1.Data-signal, R1.Pin_0
  5V_2: Part2.5V, RHT1.Vcc, R1.Pin_1

custom parts:
  ESP8266 WiFi Module: Generic WiFi Module based on the ESP8266 with onboard PCB antenna and UART communications
  Fan - Ventilador: Ventilador de 2 pines, se encuentra comunmente en computadoras de escritorio
